// Logisim project Game.circ as structural Verilog
module main (
);

  wire clock;
  wire [31:0] asteroidcontroller_1_out_1, cascada_1_out_2, cascada_1_out_3, cascada_1_out_4, cascada_1_out_5,
       cascada_1_out_6, cascada_1_out_7, cascada_1_out_8, cascada_1_out_9, cascada_1_out_10,
       cascada_1_out_11, cascada_1_out_12, cascada_1_out_13, cascada_1_out_14, cascada_1_out_15,
       cascada_1_out_16, cascada_1_out_17, cascada_1_out_18, cascada_1_out_19, cascada_1_out_20,
       cascada_1_out_21, cascada_1_out_22, cascada_1_out_23, cascada_1_out_24, cascada_1_out_25,
       cascada_1_out_26, cascada_1_out_27, cascada_1_out_28, cascada_1_out_29, cascada_1_out_30,
       cascada_1_out_31, cascada_1_out_32;

  Clock clock_1 (.out(clock));
  AsteroidController asteroidcontroller_1 (.out_1(asteroidcontroller_1_out_1));
  Cascada cascada_1 (
    .INPUT(asteroidcontroller_1_out_1), .out_2(cascada_1_out_2), .out_3(cascada_1_out_3),
    .out_4(cascada_1_out_4), .out_5(cascada_1_out_5), .out_6(cascada_1_out_6), .out_7(cascada_1_out_7),
    .out_8(cascada_1_out_8), .out_9(cascada_1_out_9), .out_10(cascada_1_out_10), .out_11(cascada_1_out_11),
    .out_12(cascada_1_out_12), .out_13(cascada_1_out_13), .out_14(cascada_1_out_14),
    .out_15(cascada_1_out_15), .out_16(cascada_1_out_16), .out_17(cascada_1_out_17),
    .out_18(cascada_1_out_18), .out_19(cascada_1_out_19), .out_20(cascada_1_out_20),
    .out_21(cascada_1_out_21), .out_22(cascada_1_out_22), .out_23(cascada_1_out_23),
    .out_24(cascada_1_out_24), .out_25(cascada_1_out_25), .out_26(cascada_1_out_26),
    .out_27(cascada_1_out_27), .out_28(cascada_1_out_28), .out_29(cascada_1_out_29),
    .out_30(cascada_1_out_30), .out_31(cascada_1_out_31), .out_32(cascada_1_out_32));
  DotMatrix #(.inputtype("row"), .matrixcols(32), .matrixrows(32)) dotmatrix_1 (
    .row0(cascada_1_out_2), .row1(cascada_1_out_3), .row2(cascada_1_out_4), .row3(cascada_1_out_5),
    .row4(cascada_1_out_6), .row5(cascada_1_out_7), .row6(cascada_1_out_8), .row7(cascada_1_out_9),
    .row8(cascada_1_out_10), .row9(cascada_1_out_11), .row10(cascada_1_out_12), .row11(cascada_1_out_13),
    .row12(cascada_1_out_14), .row13(cascada_1_out_15), .row14(cascada_1_out_16), .row15(cascada_1_out_17),
    .row16(cascada_1_out_18), .row17(cascada_1_out_19), .row18(cascada_1_out_20), .row19(cascada_1_out_21),
    .row20(cascada_1_out_22), .row21(cascada_1_out_23), .row22(cascada_1_out_24), .row23(cascada_1_out_25),
    .row24(cascada_1_out_26), .row25(cascada_1_out_27), .row26(cascada_1_out_28), .row27(cascada_1_out_29),
    .row28(cascada_1_out_30), .row29(cascada_1_out_31), .row30(cascada_1_out_32));  // open: row31
endmodule

module BarHandler (
  input  reset,
  input  R,
  input  L,
  output [31:0] \output 
);

  wire clock, L_t, Left, R_t, Reset_t, reset_t_t, Right, update;
  wire [31:0] divider_1_out, multiplexer_1_out, multiplexer_2_out, multiplier_1_out, register_1_q;

  Clock clock_1 (.out(clock));
  or or_1 (R_t, R, Right);
  or or_2 (L_t, L, Left);
  or or_3 (reset_t_t, reset, Reset_t);
  or or_4 (update, R_t, L_t, reset_t_t);
  Multiplexer #(.width(32)) multiplexer_1 (
    .in0(\output ), .in1(32'h38000), .out(multiplexer_1_out), .sel(reset_t_t));  // open: en
  Register #(.width(32)) register_1 (.D(multiplexer_1_out), .en(update), .Q(register_1_q), .clk(clock));  // open: clr
  DotMatrix #(.inputtype("row"), .matrixcols(32), .matrixrows(2)) dotmatrix_1 (.row1(\output ));  // open: row0
  // Probe on register_1_q
  Button button_1 (.out(Right));
  Multiplier #(.width(32)) multiplier_1 (.a(register_1_q), .b(32'h2), .out(multiplier_1_out));  // open: cin, cout
  Divider #(.width(32)) divider_1 (.a(register_1_q), .b(32'h2), .out(divider_1_out));  // open: upper, rem
  Button button_2 (.out(Left));
  Button button_3 (.out(Reset_t));
  Multiplexer #(.width(32)) multiplexer_2 (
    .in0(multiplier_1_out), .in1(divider_1_out), .out(multiplexer_2_out), .sel(R_t));  // open: en
  ColisionHandler colisionhandler_1 (.Entrada_sin_depurar(multiplexer_2_out), .Salida_depurada(\output ));

  // Other names for the same wires on the sheet: out[31:0] = \output 
endmodule

module ColisionHandler (
  input  [31:0] Entrada_sin_depurar,
  output [31:0] Salida_depurada
);

  wire comparator_1_eq, comparator_2_eq, comparator_3_eq, comparator_4_eq, comparator_5_eq, comparator_6_eq;
  wire [1:0] multiplexer_6_out, varcolision, varcolision1, varcolision2;
  wire [31:0] sal1, sal2;

  Comparator #(.width(32)) comparator_1 (
    .a(Entrada_sin_depurar), .b(32'h80000000), .eq(comparator_1_eq));  // open: gt, lt
  Comparator #(.width(32)) comparator_2 (.a(Entrada_sin_depurar), .b(32'h1), .eq(comparator_2_eq));  // open: gt, lt
  Multiplexer #(.width(32)) multiplexer_1 (
    .in0(Entrada_sin_depurar), .in1(32'h7), .out(sal1), .sel(comparator_1_eq));  // open: en
  Multiplexer #(.width(32)) multiplexer_2 (
    .in0(Entrada_sin_depurar), .in1(32'he0000000), .out(sal2), .sel(comparator_2_eq));  // open: en
  Comparator #(.width(32)) comparator_3 (.a(Entrada_sin_depurar), .b(sal1), .eq(comparator_3_eq));  // open: gt, lt
  Comparator #(.width(32)) comparator_4 (.a(Entrada_sin_depurar), .b(sal2), .eq(comparator_4_eq));  // open: gt, lt
  Multiplexer #(.width(2)) multiplexer_3 (
    .in0(2'b00), .in1(2'b10), .out(varcolision1), .sel(comparator_3_eq));  // open: en
  Multiplexer #(.width(2)) multiplexer_4 (
    .in0(2'b01), .in1(2'b10), .out(varcolision2), .sel(comparator_4_eq));  // open: en
  Multiplexer #(.select(2), .width(32)) multiplexer_5 (
    .in0(sal1), .in1(sal2), .in3(Entrada_sin_depurar), .out(Salida_depurada), .sel(varcolision));  // open: in2, en
  Multiplexer #(.width(2)) multiplexer_6 (
    .in0(varcolision2), .in1(varcolision1), .out(multiplexer_6_out), .sel(comparator_5_eq));  // open: en
  Comparator #(.width(2)) comparator_5 (.a(varcolision1), .b(2'b00), .eq(comparator_5_eq));  // open: gt, lt
  Comparator #(.width(2)) comparator_6 (.a(varcolision1), .b(varcolision2), .eq(comparator_6_eq));  // open: gt, lt
  Multiplexer #(.width(2)) multiplexer_7 (
    .in0(multiplexer_6_out), .in1(2'b11), .out(varcolision), .sel(comparator_6_eq));  // open: en

  // Other names for the same wires on the sheet: colisioninput[31:0] = Entrada_sin_depurar
endmodule

module AsteroidController (
  output [31:0] out_1
);

  wire clock, clock_1_out, t_ff_1_q, t_ff_2_q, t_ff_2_qn;
  wire [31:0] a, b, c, d, e, f;

  Clock clock_1 (.out(clock_1_out));
  T_Flip_Flop t_ff_1 (.clk(clock_1_out), .T(clock_1_out), .Q(t_ff_1_q));  // open: Qn, preset, reset, en
  T_Flip_Flop t_ff_2 (.clk(t_ff_1_q), .T(t_ff_1_q), .Q(t_ff_2_q), .Qn(t_ff_2_qn));  // open: preset, reset, en
  T_Flip_Flop t_ff_3 (.clk(t_ff_2_qn), .T(t_ff_2_qn), .Q(clock));  // open: Qn, preset, reset, en
  Random #(.width(32)) random_1 (.clk(clock_1_out), .out(a));  // open: next, clr
  Random #(.width(32)) random_2 (.clk(clock_1_out), .out(b));  // open: next, clr
  Random #(.width(32), .trigger("falling")) random_3 (.clk(t_ff_1_q), .out(c));  // open: next, clr
  Random #(.width(32)) random_4 (.clk(t_ff_1_q), .out(d));  // open: next, clr
  Random #(.width(32)) random_5 (.clk(t_ff_2_q), .out(e));  // open: next, clr
  Random #(.width(32)) random_6 (.clk(t_ff_2_q), .out(f));  // open: next, clr
  assign out_1 = a & b & c & d & e & f;  // AND_Gate and_1, 32 bits wide
  DotMatrix #(.inputtype("row"), .matrixcols(32), .matrixrows(2)) dotmatrix_1 (.row0(out_1));  // open: row1
endmodule

module Cascada (
  input  [31:0] INPUT,
  output [31:0] out_2,
  output [31:0] out_3,
  output [31:0] out_4,
  output [31:0] out_5,
  output [31:0] out_6,
  output [31:0] out_7,
  output [31:0] out_8,
  output [31:0] out_9,
  output [31:0] out_10,
  output [31:0] out_11,
  output [31:0] out_12,
  output [31:0] out_13,
  output [31:0] out_14,
  output [31:0] out_15,
  output [31:0] out_16,
  output [31:0] out_17,
  output [31:0] out_18,
  output [31:0] out_19,
  output [31:0] out_20,
  output [31:0] out_21,
  output [31:0] out_22,
  output [31:0] out_23,
  output [31:0] out_24,
  output [31:0] out_25,
  output [31:0] out_26,
  output [31:0] out_27,
  output [31:0] out_28,
  output [31:0] out_29,
  output [31:0] out_30,
  output [31:0] out_31,
  output [31:0] out_32
);

  wire clock;

  Clock clock_1 (.out(clock));
  Register #(.width(32)) register_1 (.D(INPUT), .Q(out_2), .clk(clock));  // open: en, clr
  Register #(.width(32)) register_2 (.D(out_7), .Q(out_8), .clk(clock));  // open: en, clr
  Register #(.width(32)) register_3 (.D(out_13), .Q(out_14), .clk(clock));  // open: en, clr
  Register #(.width(32)) register_4 (.D(out_19), .Q(out_20), .clk(clock));  // open: en, clr
  Register #(.width(32)) register_5 (.D(out_25), .Q(out_26), .clk(clock));  // open: en, clr
  Register #(.width(32)) register_6 (.D(out_31), .Q(out_32), .clk(clock));  // open: en, clr
  Register #(.width(32)) register_7 (.D(out_2), .Q(out_3), .clk(clock));  // open: en, clr
  Register #(.width(32)) register_8 (.D(out_8), .Q(out_9), .clk(clock));  // open: en, clr
  Register #(.width(32)) register_9 (.D(out_14), .Q(out_15), .clk(clock));  // open: en, clr
  Register #(.width(32)) register_10 (.D(out_20), .Q(out_21), .clk(clock));  // open: en, clr
  Register #(.width(32)) register_11 (.D(out_26), .Q(out_27), .clk(clock));  // open: en, clr
  Register #(.width(32)) register_12 (.D(out_3), .Q(out_4), .clk(clock));  // open: en, clr
  Register #(.width(32)) register_13 (.D(out_9), .Q(out_10), .clk(clock));  // open: en, clr
  Register #(.width(32)) register_14 (.D(out_15), .Q(out_16), .clk(clock));  // open: en, clr
  Register #(.width(32)) register_15 (.D(out_21), .Q(out_22), .clk(clock));  // open: en, clr
  Register #(.width(32)) register_16 (.D(out_27), .Q(out_28), .clk(clock));  // open: en, clr
  Register #(.width(32)) register_17 (.D(out_4), .Q(out_5), .clk(clock));  // open: en, clr
  Register #(.width(32)) register_18 (.D(out_10), .Q(out_11), .clk(clock));  // open: en, clr
  Register #(.width(32)) register_19 (.D(out_16), .Q(out_17), .clk(clock));  // open: en, clr
  Register #(.width(32)) register_20 (.D(out_22), .Q(out_23), .clk(clock));  // open: en, clr
  Register #(.width(32)) register_21 (.D(out_28), .Q(out_29), .clk(clock));  // open: en, clr
  Register #(.width(32)) register_22 (.D(out_5), .Q(out_6), .clk(clock));  // open: en, clr
  Register #(.width(32)) register_23 (.D(out_11), .Q(out_12), .clk(clock));  // open: en, clr
  Register #(.width(32)) register_24 (.D(out_17), .Q(out_18), .clk(clock));  // open: en, clr
  Register #(.width(32)) register_25 (.D(out_23), .Q(out_24), .clk(clock));  // open: en, clr
  Register #(.width(32)) register_26 (.D(out_29), .Q(out_30), .clk(clock));  // open: en, clr
  Register #(.width(32)) register_27 (.D(out_6), .Q(out_7), .clk(clock));  // open: en, clr
  Register #(.width(32)) register_28 (.D(out_12), .Q(out_13), .clk(clock));  // open: en, clr
  Register #(.width(32)) register_29 (.D(out_18), .Q(out_19), .clk(clock));  // open: en, clr
  Register #(.width(32)) register_30 (.D(out_24), .Q(out_25), .clk(clock));  // open: en, clr
  Register #(.width(32)) register_31 (.D(out_30), .Q(out_31), .clk(clock));  // open: en, clr
endmodule

// 1
module respaldo (
);

  wire CLOCK, clock_t, comparator_1_eq, comparator_2_eq, keyboard_1_avail, L, LEFT, R, Reset, RIGHT,
       t_ff_1_q, t_ff_2_q, t_ff_2_qn, update;
  wire [6:0] keyboard_1_data, register_32_q;
  wire [31:0] _1, _2, _3, _4, _5, _6, _7, _8, _9, _10, _11, _12, _13, _14, _15, _16, _17, _18, _19, _20, _21,
       _22, _23, _24, _25, _26, _27, _28, _29, _30, _31, a, and_1_out, b, c, d, divider_1_out, e, f,
       multiplexer_1_out, multiplexer_2_out, multiplier_1_out, out, register_33_q;

  Clock clock_1 (.out(CLOCK));
  T_Flip_Flop t_ff_1 (.clk(CLOCK), .T(CLOCK), .Q(t_ff_1_q));  // open: Qn, preset, reset, en
  T_Flip_Flop t_ff_2 (.clk(t_ff_1_q), .T(t_ff_1_q), .Q(t_ff_2_q), .Qn(t_ff_2_qn));  // open: preset, reset, en
  T_Flip_Flop t_ff_3 (.clk(t_ff_2_qn), .T(t_ff_2_qn), .Q(clock_t));  // open: Qn, preset, reset, en
  T_Flip_Flop t_ff_4 (.clk(clock_t), .T(clock_t));  // open: Q, Qn, preset, reset, en
  Register #(.width(32)) register_1 (.D(and_1_out), .Q(_1), .clk(clock_t));  // open: en, clr
  Register #(.width(32)) register_2 (.D(_8), .Q(_9), .clk(clock_t));  // open: en, clr
  Register #(.width(32)) register_3 (.D(_16), .Q(_17), .clk(clock_t));  // open: en, clr
  Register #(.width(32)) register_4 (.D(_24), .Q(_25), .clk(clock_t));  // open: en, clr
  BarHandler barhandler_1 (.L(t_ff_2_qn));  // open: reset, R, output
  Register #(.width(32)) register_5 (.D(_1), .Q(_2), .clk(clock_t));  // open: en, clr
  Register #(.width(32)) register_6 (.D(_9), .Q(_10), .clk(clock_t));  // open: en, clr
  Register #(.width(32)) register_7 (.D(_17), .Q(_18), .clk(clock_t));  // open: en, clr
  Register #(.width(32)) register_8 (.D(_25), .Q(_26), .clk(clock_t));  // open: en, clr
  Random #(.width(32)) random_1 (.clk(CLOCK), .out(a));  // open: next, clr
  Random #(.width(32)) random_2 (.out(b));  // open: clk, next, clr
  Random #(.width(32), .trigger("falling")) random_3 (.clk(t_ff_1_q), .out(c));  // open: next, clr
  Random #(.width(32)) random_4 (.clk(t_ff_1_q), .out(d));  // open: next, clr
  Random #(.width(32)) random_5 (.clk(t_ff_2_q), .out(e));  // open: next, clr
  Random #(.width(32)) random_6 (.clk(t_ff_2_q), .out(f));  // open: next, clr
  Register #(.width(32)) register_9 (.D(_2), .Q(_3), .clk(clock_t));  // open: en, clr
  Register #(.width(32)) register_10 (.D(_10), .Q(_11), .clk(clock_t));  // open: en, clr
  Register #(.width(32)) register_11 (.D(_18), .Q(_19), .clk(clock_t));  // open: en, clr
  Register #(.width(32)) register_12 (.D(_26), .Q(_27), .clk(clock_t));  // open: en, clr
  Register #(.width(32)) register_13 (.D(_3), .Q(_4), .clk(clock_t));  // open: en, clr
  Register #(.width(32)) register_14 (.D(_11), .Q(_12), .clk(clock_t));  // open: en, clr
  Register #(.width(32)) register_15 (.D(_19), .Q(_20), .clk(clock_t));  // open: en, clr
  Register #(.width(32)) register_16 (.D(_27), .Q(_28), .clk(clock_t));  // open: en, clr
  // Probe on and_1_out
  assign and_1_out = a & b & c & d & e & f;  // AND_Gate and_1, 32 bits wide
  Register #(.width(32)) register_17 (.D(_4), .Q(_5), .clk(clock_t));  // open: en, clr
  Register #(.width(32)) register_18 (.D(_12), .Q(_13), .clk(clock_t));  // open: en, clr
  Register #(.width(32)) register_19 (.D(_20), .Q(_21), .clk(clock_t));  // open: en, clr
  Register #(.width(32)) register_20 (.D(_28), .Q(_29), .clk(clock_t));  // open: en, clr
  Register #(.width(32)) register_21 (.D(_5), .Q(_6), .clk(clock_t));  // open: en, clr
  Register #(.width(32)) register_22 (.D(_13), .Q(_14), .clk(clock_t));  // open: en, clr
  Register #(.width(32)) register_23 (.D(_21), .Q(_22), .clk(clock_t));  // open: en, clr
  Register #(.width(32)) register_24 (.D(_29), .Q(_30), .clk(clock_t));  // open: en, clr
  DotMatrix #(.inputtype("row"), .matrixcols(32), .matrixrows(32)) dotmatrix_1 (
    .row0(_1), .row1(_2), .row2(_3), .row3(_4), .row4(_5), .row5(_6), .row6(_7), .row7(_8), .row8(_9),
    .row9(_10), .row10(_11), .row11(_12), .row12(_13), .row13(_14), .row14(_15), .row15(_16), .row16(_17),
    .row17(_18), .row18(_19), .row19(_20), .row20(_21), .row21(_22), .row22(_23), .row23(_24), .row24(_25),
    .row25(_26), .row26(_27), .row27(_28), .row28(_29), .row29(_30), .row30(_31), .row31(out));
  Button u_RESET (.out(Reset));
  Register #(.width(32)) register_25 (.D(_6), .Q(_7), .clk(clock_t));  // open: en, clr
  Register #(.width(32)) register_26 (.D(_14), .Q(_15), .clk(clock_t));  // open: en, clr
  Register #(.width(32)) register_27 (.D(_22), .Q(_23), .clk(clock_t));  // open: en, clr
  Register #(.width(32)) register_28 (.D(_30), .Q(_31), .clk(clock_t));  // open: en, clr
  Button button_1 (.out(LEFT));
  Keyboard keyboard_1 (.clk(CLOCK), .avail(keyboard_1_avail), .data(keyboard_1_data));  // open: re, clr
  Register #(.width(32)) register_29 (.D(_7), .Q(_8), .clk(clock_t));  // open: en, clr
  Register #(.width(32)) register_30 (.D(_15), .Q(_16), .clk(clock_t));  // open: en, clr
  Register #(.width(32)) register_31 (.D(_23), .Q(_24), .clk(clock_t));  // open: en, clr
  Button button_2 (.out(RIGHT));
  Comparator #(.width(7)) comparator_1 (.a(keyboard_1_data), .b(7'b1100001), .eq(comparator_1_eq));  // open: gt, lt
  // Probe on register_32_q
  Register #(.width(7)) register_32 (.D(keyboard_1_data), .Q(register_32_q), .clk(keyboard_1_avail));  // open: en, clr
  Multiplexer #(.width(32)) multiplexer_1 (
    .in0(out), .in1(32'h38000), .out(multiplexer_1_out), .sel(Reset));  // open: en
  Register #(.width(32)) register_33 (.D(multiplexer_1_out), .en(update), .Q(register_33_q), .clk(CLOCK));  // open: clr
  Comparator #(.width(7)) comparator_2 (.a(keyboard_1_data), .b(7'b1100100), .eq(comparator_2_eq));  // open: gt, lt
  // Probe on register_33_q
  or or_1 (R, comparator_2_eq, RIGHT);
  or or_2 (L, comparator_1_eq, LEFT);
  Multiplier #(.width(32)) multiplier_1 (.a(register_33_q), .b(32'h2), .out(multiplier_1_out));  // open: cin, cout
  Divider #(.width(32)) divider_1 (.a(register_33_q), .b(32'h2), .out(divider_1_out));  // open: upper, rem
  or or_3 (update, R, L, Reset);
  Multiplexer #(.width(32)) multiplexer_2 (
    .in0(multiplier_1_out), .in1(divider_1_out), .out(multiplexer_2_out), .sel(R));  // open: en
  // Probe on _1
  // Probe on _2
  // Probe on _3
  // Probe on _4
  // Probe on _5
  // Probe on _6
  // Probe on _7
  // Probe on _8
  // Probe on _9
  // Probe on _10
  // Probe on _11
  // Probe on _12
  // Probe on _13
  // Probe on _14
  // Probe on _15
  // Probe on _16
  // Probe on _17
  // Probe on _18
  // Probe on _19
  // Probe on _20
  // Probe on _21
  // Probe on _22
  // Probe on _23
  // Probe on _24
  // Probe on _25
  // Probe on _26
  // Probe on _27
  // Probe on _28
  // Probe on _29
  // Probe on _30
  // Probe on _31
  ColisionHandler colisionhandler_1 (.Entrada_sin_depurar(multiplexer_2_out), .Salida_depurada(out));

  // Notes on the sheet:
  //   CONTROLES:
  //   a <-  -> d
endmodule

module KeyBoardHandler (
);

  wire clock, keyboard_1_avail, left, right;
  wire [6:0] keyboard_1_data, register_1_q;

  Clock clock_1 (.out(clock));
  Keyboard keyboard_1 (.clk(clock), .avail(keyboard_1_avail), .data(keyboard_1_data));  // open: re, clr
  Comparator #(.width(7)) comparator_1 (.a(keyboard_1_data), .b(7'b1100001), .eq(left));  // open: gt, lt
  // Probe on register_1_q
  Register #(.width(7)) register_1 (.D(keyboard_1_data), .Q(register_1_q), .clk(keyboard_1_avail));  // open: en, clr
  Comparator #(.width(7)) comparator_2 (.a(keyboard_1_data), .b(7'b1100100), .eq(right));  // open: gt, lt
endmodule
